# Fritzing sketch Esquematico Fritzing_receptor (saved by Fritzing 0.9.3b)
breadboards: 1

parts:
  U1 = ESP8266 WiFi Module [part_number=ESP8266]
  IC1 = L293D [package=THT]
  LED1 = LEDs [package=led10mm]
  Y1 = CRYSTAL [package=hc49up]
  C1 = Tantalum Capacitor [capacitance=1μF package="100 mil [THT, tantalum]"]
  Atmega1 = ATmega328 [package=tqfp]
  C2 = Tantalum Capacitor [capacitance=1μF package="100 mil [THT, tantalum]"]
  M1 = Stepper Motor - Bipolar
  U2 = RELAY [package=relay-t9a]
  SP1 = SPEAKER [package=pcb_mount_speaker]

nets:
  N1: U1.RXD, Atmega1.PD0(RXD)
  N2: U1.VCC, IC1.+V, Atmega1.AVCC
  N3: U1.TXD, Atmega1.PD1(TXD)
  N4: IC1.Enable_1, Atmega1.PB3(MOSI_OC2)
  N5: IC1.Out_1_(_Controlled_by_Enable_1_), M1.A
  N6: IC1.0V, Y1.1, Atmega1.PB6(XTAL1_TOSC1), C2.-, M1.D, U2.COIL2
  N7: IC1.Enable_2, Atmega1.PB2(SS_OC1B)
  N8: IC1.Out_3_(_Controlled_by_Enable_2_), M1.C
  N9: LED1.C, U2.NC, SP1.+
  N10: LED1.A, U2.NO, SP1.-
  N11: Y1.2, C1.+, Atmega1.PB7(XTAL2_TOSC2)
  N12: C1.-, C2.+
  N13: Atmega1.PC0(ADC0), U2.COIL1
