# Fritzing sketch Esquematico Fritzing_transmisor (saved by Fritzing 0.9.3b)
breadboards: 1

parts:
  Raspberry_Pi_1 = Raspberry Pi 3 [part_number=RPI-3-V1.2]
  hc-sr1 = hc-sr04
  DS1 = DS18B20 1-Wire Temperature Sensor [part_number=DS18B20]
  R1 = Resistor [tolerance=±5% resistance=1k package="0603 [SMD]"]
  R2 = Resistor [tolerance=±5% resistance=1k package="0603 [SMD]"]
  R3 = Resistor [tolerance=±5% resistance=1k package="0603 [SMD]"]
  R4 = Resistor [tolerance=±5% resistance=4.7k package="0603 [SMD]"]
  R5 = Resistor [tolerance=±5% resistance=330 package="0603 [SMD]"]
  LED1 = smd LED [color="Red (633nm)" package="1206 [SMD]"]

nets:
  N1: Raspberry_Pi_1.GPIO4, DS1.DQ, R4.Pin_0
  N2: Raspberry_Pi_1.GPIO13, R1.Pin_1, R2.Pin_1, R3.Pin_0
  GND: Raspberry_Pi_1.GND, hc-sr1.GND, DS1.GND, R3.Pin_1, LED1.cathode
  N3: Raspberry_Pi_1.GPIO12, hc-sr1.Trig
  N4: Raspberry_Pi_1.GPIO24, R5.Pin_1
  5V: Raspberry_Pi_1.5V, hc-sr1.VCC, DS1.VDD, R4.Pin_1
  N5: hc-sr1.Echo, R1.Pin_0, R2.Pin_0
  N6: R5.Pin_0, LED1.anode
